# Fritzing sketch Circuito esquemático da bengala (saved by Fritzing 0.9.3b)
breadboards: 1

parts:
  VCC1 = Battery block 9V
  U3 = SWITCH_SPDT [package=kps-1290]
  Componente2 = Arduino Nano (Rev3.0) (ICSP)
  R1 = Resistor [tolerance=±5% resistance=10k package=THT]
  R2 = Resistor [tolerance=±5% resistance=10k package=THT]
  R3 = Resistor [tolerance=±5% resistance=220 package=THT]
  J1 = Piezo Speaker
  R4 = Resistor [tolerance=±5% resistance=1.5k package=THT]
  D1 = Rectifier Diode [part_number=1N4001 package="Melf DO-213 AB [SMD]"]
  C2 = Ceramic Capacitor [capacitance=1µF package="100 mil [THT, multilayer]"]
  Q2 = NPN-Transistor [package="TO92 [THT]"]
  U4 = Vibration Motor- ROB-08449 [package=vibe-motor-10mm]
  hc-sr1 = hc-sr04

nets:
  GND: VCC1.-, Componente2.GND, J1.pin2, Q2.E, hc-sr1.GND
  N1: VCC1.+, U3.S, R1.Pin_0
  N2: U3.P, Componente2.VIN
  N3: Componente2.D2, Componente2.D4, Componente2.5V, hc-sr1.Trig
  N4: Componente2.D6, R4.Pin_0
  N5: Componente2.D8, R3.Pin_1
  N6: Componente2.A5, R2.Pin_1
  N7: Componente2.3V3, D1.cathode, C2.1, U4.+
  N8: R1.Pin_1, R2.Pin_0
  N9: R3.Pin_0, J1.pin1
  N10: R4.Pin_1, Q2.B
  N11: D1.anode, C2.0, Q2.C, U4.-
